// Logisim project DigitalBlockFinalll.circ as structural Verilog: 1 circuit, main circuit main
module main (
  input  A0,
  input  A1,
  input  A2,
  input  A3,
  input  B0,
  input  B1,
  input  B2,
  input  B3,
  input  [2:0] in_9,
  output out_10
);

  wire and_1_out, and_2_out, and_3_out, and_4_out, multiplexer_1_out, multiplexer_2_out, multiplexer_3_out,
       multiplexer_4_out, nor_1_out, nor_2_out, nor_3_out, nor_4_out, or_1_out, or_2_out, or_3_out, or_4_out,
       xor_1_out, xor_2_out, xor_3_out, xor_4_out;

  and and_1 (and_1_out, B0, A0);
  or or_1 (or_1_out, B0, A0);
  nor nor_1 (nor_1_out, B0, A0);
  Multiplexer #(.select(3), .enable("false")) multiplexer_1 (
    .in0(and_1_out), .in1(or_1_out), .in2(nor_1_out), .in3(xor_1_out), .in4(1'b0), .in5(A1), .in6(A0),
    .in7(B3), .out(multiplexer_1_out), .sel(in_9));
  xor xor_1 (xor_1_out, B0, A0);
  and and_2 (and_2_out, B1, A1);
  or or_2 (or_2_out, B1, A1);
  Multiplexer #(.select(3), .enable("false")) multiplexer_2 (
    .in0(and_2_out), .in1(or_2_out), .in2(nor_2_out), .in3(xor_2_out), .in4(A0), .in5(A3), .in6(A0),
    .in7(A0), .out(multiplexer_2_out), .sel(in_9));
  xor xor_2 (xor_2_out, B1, A1);
  nor nor_2 (nor_2_out, B1, A1);
  and and_3 (and_3_out, B2, A1);
  nor nor_3 (nor_3_out, B2, A1);
  or or_3 (or_3_out, B2, A1);
  Multiplexer #(.select(3), .enable("false")) multiplexer_3 (
    .in0(and_3_out), .in1(or_3_out), .in2(nor_3_out), .in3(xor_3_out), .in4(A1), .in5(A3), .in6(A1),
    .in7(A1), .out(multiplexer_3_out), .sel(in_9));
  xor xor_3 (xor_3_out, B2, A1);
  and and_4 (and_4_out, B3, A3);
  or or_4 (or_4_out, B3, A3);
  nor nor_4 (nor_4_out, B3, A3);
  Multiplexer #(.select(3), .enable("false")) multiplexer_4 (
    .in0(and_4_out), .in1(or_4_out), .in2(nor_4_out), .in3(xor_4_out), .in4(A1), .in5(1'b0), .in6(A1),
    .in7(B3), .out(multiplexer_4_out), .sel(in_9));
  xor xor_4 (xor_4_out, B3, A3);
  nor nor_5 (out_10, multiplexer_4_out, multiplexer_3_out, multiplexer_1_out, multiplexer_2_out);

  assign A2 = A1;
endmodule
