// Logisim project schematic_rev2.circ as structural Verilog: 1 circuit, main circuit main
module main (
  input  A1,
  input  A2,
  input  A3,
  input  A4,
  input  B1,
  input  B2,
  input  B3,
  input  B4,
  input  OP1,
  input  OP2,
  input  OP3,
  output O1,
  output O2,
  output O3,
  output O4,
  output Zero
);

  wire n7402_1_p1, n7402_1_p4, n7402_1_p9, n7402_1_p12, n7408_1_p3, n7408_1_p6, n7408_1_p10, n7432_1_p4,
       n7432_1_p7, n7432_1_p9, n7432_1_p13, n7432_1_p16, n7486_1_p3, n7486_1_p6, n7486_1_p11, n7486_1_p14;

  // _7408 7408_1: pin names not known; wires that end beside it: A1, B1, n7408_1_p3, A2, B2, n7408_1_p6, 1'b1, A3, B3, n7408_1_p10, A4, B4
  // _7432 7432_1: pin names not known; wires that end beside it: 1'b0, A1, B1, n7432_1_p4, B2, A2, n7432_1_p7, 1'b0, n7432_1_p9, 1'b1, A3, B3, n7432_1_p13, A4, B4, n7432_1_p16
  // _7402 7402_1: pin names not known; wires that end beside it: n7402_1_p1, A1, B1, n7402_1_p4, A2, B2, 1'b0, 1'b1, n7402_1_p9, A3, B3, n7402_1_p12, A4, B4
  // _7486 7486_1: pin names not known; wires that end beside it: A1, B1, n7486_1_p3, A2, B2, n7486_1_p6, 1'b0, 1'b1, A3, B3, n7486_1_p11, A4, B4, n7486_1_p14
  // _74151 74151_1: pin names not known; wires that end beside it: n7402_1_p1, n7486_1_p3, n7432_1_p4, n7408_1_p3, O1, 1'b1, 1'b0, A1, B2, A2
  // _74151 74151_2: pin names not known; wires that end beside it: 1'b0, n7402_1_p4, n7486_1_p6, n7432_1_p7, n7408_1_p6, O2, OP3, OP2, OP1, 1'b1, A1, A1, B3, A3
  // _74151 74151_3: pin names not known; wires that end beside it: 1'b0, 1'b0, n7402_1_p9, n7486_1_p11, n7432_1_p13, n7408_1_p10, O3, OP3, OP2, OP1, 1'b1, A2, A2, B4, A4
  // _74151 74151_4: pin names not known; wires that end beside it: 1'b0, n7402_1_p12, n7486_1_p14, n7432_1_p16, n7432_1_p9, O4, 1'b0, 1'b0, OP3, OP2, OP1, 1'b1, A3, A3, B1, 1'b0, OP3, OP2, OP1
  // _7425 7425_1: pin names not known; wires that end beside it: 1'b0, 1'b1, O1, O2, O3, O4, Zero
endmodule
